# Fritzing sketch FEM-MUSina-fritzing-project (saved by Fritzing 0.9.0b)
circuit board: 7.33904cm x 5.60464cm

parts:
  R1 = Resistor [tolerance=±5% resistance=220 package=THT]
  JP5 = Header 3 [package=screwterminal-3.5mm-3_lock.007s]
  JP6 = Header 4 [package=screwterminal-3.5mm-4_lock]  # not connected
  End_Switch = Screw terminal - 2 pins [package=THT]
  12V_DC = Power plug
  Pump = Screw terminal - 2 pins [package=THT]
  JP4 = Header 3 [package=screwterminal-3.5mm-3_lock.007s]
  IRF520 = Basic FET N-Channel [package="TO220 [THT]"]
  74HC4051 = 4051 Analog Multiplexor [chip_label=4051 package="DIP (Dual Inline) [THT]"]
  Componente1 = Arduino Uno (Rev3)
  R2 = Resistor [tolerance=±5% resistance=10k package=THT]
  J1 = Basic Servo
  Servo_Motor = female pin header, 3 pins [form="♀ (female)"]
  Servo = rounded female pin header, 3 pins [form="♀ (female rounded)"]
  S1 = Pushbutton [package=THT]
  M1 = DC Motor

nets (from the schematic view):
  N1: R1.Pin_0, 74HC4051.A, Componente1.A5/SCL
  VCC: R1.Pin_1, End_Switch.pin2, 74HC4051.VCC, Componente1.5V, J1.vcc, Servo_Motor.pin3, Servo.pin3, S1.leg0
  Probe 7: JP5.3
  N2: End_Switch.pin1, Componente1.D2, R2.Pin_0, S1.leg1
  N3: 12V_DC.GND, R2.Pin_1
  N4: 12V_DC.VCC, Pump.pin1, M1.pin_1
  N5: Pump.pin2, IRF520.source, M1.pin_2
  GND/Probe GND: JP4.2, IRF520.drain, 74HC4051.VEE, Componente1.GND, J1.gnd, Servo_Motor.pin1, Servo.pin1
  N6: IRF520.gate, Componente1.D4
  Probe 5: 74HC4051.A4
  Probe 8: 74HC4051.A7
  Probe 6: 74HC4051.A5
  N7: 74HC4051.E, 74HC4051.GND
  N8: 74HC4051.S2, Componente1.D5_PWM
  N9: 74HC4051.S1, Componente1.D6_PWM
  N10: 74HC4051.S0, Componente1.D7
  Probe 4: 74HC4051.A3
  Probe 1: 74HC4051.A0
  Probe 2: 74HC4051.A1
  Probe 3: 74HC4051.A2
  N11: Componente1.D10_PWM/SS, J1.pulse, Servo_Motor.pin2, Servo.pin2

custom parts:
  4051 Analog Multiplexor: DIP-form factor 8-channel analog multiplexor/demultiplexor, 54HC4051
